# Fritzing sketch preamp (saved by Fritzing 0.8.3b)
breadboards: 1

parts:
  tl072 = IC, DIP package, 8 pins [chip_label=IC]
  VCC1 = Battery block 9V
  R1 = Resistor [tolerance=±5% resistance=47k package=THT]
  R2 = Resistor [tolerance=±5% resistance=47k package=THT]
  TRS1 = Audio Jack (TRS) 3.5mm [package="4Ucon 08780 [THT]"]
  C1 = Tantalum Capacitor [capacitance=10µF voltage=16V package="100 mil [THT, tantalum]"]
  C2 = Tantalum Capacitor [capacitance=10µF voltage=16V package="100 mil [THT, tantalum]"]
  S1 = Toggle Switch [package=THT]
  S2 = Toggle Switch [package=THT]
  S3 = Toggle Switch [package=THT]
  R3 = Resistor [tolerance=±5% resistance=10k package=THT]
  R4 = Resistor [tolerance=±5% resistance=10k package=THT]
  R5 = Resistor [tolerance=±5% resistance=47k package=THT]
  R6 = Resistor [tolerance=±5% resistance=47k package=THT]
  MIC1 = Microphone
  MIC2 = Microphone
  R7 = Resistor [tolerance=±5% resistance=1k package=THT]
  R8 = Resistor [tolerance=±5% resistance=1k package=THT]
  C3 = Tantalum Capacitor [capacitance="1 μF" package="100 mil [THT, tantalum]"]
  C4 = Tantalum Capacitor [capacitance="1 μF" package="100 mil [THT, tantalum]"]
  R9 = Resistor [tolerance=±5% resistance=1k package=THT]
  R10 = Resistor [tolerance=±5% resistance=1k package=THT]
  MIC3 = Microphone
  MIC4 = Microphone

nets:
  N1: tl072.pin1, C2.+, S3.COM
  N2: tl072.pin2, R4.Pin_0, R6.Pin_1, R9.Pin_0
  N3: tl072.pin3, tl072.pin5, R1.Pin_1, R2.Pin_0
  N4: tl072.pin4, R2.Pin_1, TRS1.Sleeve, S1.COM, MIC1.pin1, MIC2.pin1, MIC3.pin1, MIC4.pin1
  N5: tl072.pin6, R3.Pin_0, R5.Pin_1, R10.Pin_0
  N6: tl072.pin7, C1.+, S2.COM
  N7: tl072.pin8, VCC1.+, R1.Pin_0, R7.Pin_0, R8.Pin_0
  N8: VCC1.-, S1.L1
  N9: TRS1.Ring, C1.-
  N10: TRS1.Tip, C2.-
  N11: S2.L1, R3.Pin_1
  N12: S2.L2, R5.Pin_0
  N13: S3.L1, R4.Pin_1
  N14: S3.L2, R6.Pin_0
  N15: MIC1.pin2, R8.Pin_1, C3.+, MIC3.pin2
  N16: MIC2.pin2, R7.Pin_1, C4.+, MIC4.pin2
  N17: C3.-, R9.Pin_1
  N18: C4.-, R10.Pin_1
